# Fritzing sketch LEDTreppe (saved by Fritzing 0.9.3b)
breadboards: 1
stripboards: 1

parts:
  Bauteil1 = Arduino Uno (Rev3)
  NEOPIXEL1 = Neopixel Strip -- Black (60/m)
  5V = Power plug
  part = Resistor [tolerance=±5% resistance=740 package=THT]
  part_2 = Electrolytic Capacitor [capacitance=1mF voltage=6.3V package="200 mil [THT, electrolytic]"]
  IR1 = TSOP312.., 314.. [package=THT]
  D1 = LTE-302 [package=lte-302]
  (TODO!) = Resistor [tolerance=±5% resistance=220 package=THT]
  (TODO!)_2 = Resistor [tolerance=±5% resistance=220 package=THT]

nets:
  N1: Bauteil1.D2, IR1.Data
  N2: Bauteil1.D3_PWM, D1.A
  N3: Bauteil1.D6_PWM, part.Pin_0
  GND: Bauteil1.GND, NEOPIXEL1.GND, 5V.GND, part_2.-, IR1.GND, (TODO!).Pin_1
  VIN: Bauteil1.VIN, NEOPIXEL1.DI, 5V.VCC, part_2.+, (TODO!)_2.Pin_1
  N4: NEOPIXEL1.+5V, part.Pin_1
  N5: D1.C, (TODO!).Pin_0

custom parts:
  Neopixel Strip -- Black (60/m): Neopixel Strip, Black, 60 pixels per meter.
